# Fritzing sketch decoder (saved by Fritzing 0.8.7b)
circuit board: 7.11915cm x 5.73651cm
breadboards: 1

parts:
  Part1 = Arduino Uno (Rev3)
  IC1 = L293D [package=THT]
  start = screw terminal, 2 pins
  R1 = Resistor [tolerance=±5% resistance=10k package=THT]
  back = screw terminal, 2 pins
  R2 = Resistor [tolerance=±5% resistance=10k package=THT]
  front = screw terminal, 2 pins
  R3 = Resistor [tolerance=±5% resistance=10k package=THT]
  motor = Screw terminal - 2 pins [package=THT]
  C1 = Ceramic Capacitor [capacitance=0.1µF package="100 mil [THT, multilayer]"]
  C2 = Ceramic Capacitor [capacitance=0.1µF package="100 mil [THT, multilayer]"]
  C4 = Electrolytic Capacitor [capacitance=4.7µF voltage=16V part_number=100uf package="100 mil [THT, electrolytic]"]
  sharp = screw terminal, 3 pins
  C5 = Ceramic Capacitor [capacitance=0.1nF part_number=102 package="100 mil [THT, multilayer]"]
  Power_plug1 = Power plug - mod

nets:
  N1: Part1.A0, sharp.pin1
  N2: Part1.D8, IC1.In_1
  N3: Part1.D9_PWM, IC1.In_2
  N4: Part1.D2, start.pin1, R1.Pin_0
  N5: Part1.D4, back.pin1, R2.Pin_0
  N6: Part1.D7, front.pin1, R3.Pin_0
  N7: Part1.5V, IC1.Enable_1, IC1.+V, start.pin2, back.pin2, front.pin2, sharp.pin3, C5.1
  GND: Part1.GND, IC1.0V, R1.Pin_1, R2.Pin_1, R3.Pin_1, C1.0, C2.1, C4.-, sharp.pin2, C5.0, Power_plug1.GND
  N8: IC1.Out_1_(_Controlled_by_Enable_1_), motor.pin1, C1.1
  N9: IC1.Out_2_(_Controlled_by_Enable_1_), motor.pin2, C2.0
  N10: IC1.+Vmotor, C4.+, Power_plug1.VCC

notes:
  [+ - s]
  decoder v 0.2
  mz
  2014

custom parts:
  Power plug - mod: power plug
