# Fritzing sketch IR_receiver (saved by Fritzing 0.8.7b)
circuit board: 5.14617cm x 4.63377cm
breadboards: 1

parts:
  LED1 = LED - 3mm [color="Infrared (940nm)" package="3 mm [THT]"]
  R1 = Resistor [tolerance=±5% resistance=220 package=THT]
  LED2 = LED - 3mm [color="Infrared (940nm)" package="3 mm [THT]"]
  R2 = Resistor [tolerance=±5% resistance=220 package=THT]
  LED3 = LED - 3mm [color="Infrared (940nm)" package="3 mm [THT]"]
  R3 = Resistor [tolerance=±5% resistance=220 package=THT]
  LED4 = LED - 3mm [color="Infrared (940nm)" package="3 mm [THT]"]
  R4 = Resistor [tolerance=±5% resistance=220 package=THT]
  LED5 = LED - 3mm [color="Infrared (940nm)" package="3 mm [THT]"]
  R5 = Resistor [tolerance=±5% resistance=220 package=THT]
  LED6 = LED - 3mm [color="Infrared (940nm)" package="3 mm [THT]"]
  R6 = Resistor [tolerance=±5% resistance=220 package=THT]
  J2 = screw terminal, 8 pins

nets:
  N1: LED1.cathode, LED2.cathode, LED3.cathode, LED4.cathode, LED5.cathode, LED6.cathode, J2.pin8
  N2: LED1.anode, R1.Pin_1, J2.pin1
  N3: R1.Pin_0, R2.Pin_0, R3.Pin_0, R4.Pin_0, R5.Pin_0, R6.Pin_0, J2.pin7
  N4: LED2.anode, R2.Pin_1, J2.pin2
  N5: LED3.anode, R3.Pin_1, J2.pin3
  N6: LED4.anode, R4.Pin_1, J2.pin4
  N7: LED5.anode, R5.Pin_1, J2.pin5
  N8: LED6.anode, R6.Pin_1, J2.pin6
