# Fritzing sketch shield (saved by Fritzing 0.8.7b)
circuit board: 7.92948cm x 5.59434cm
breadboards: 1

parts:
  Part1 = Arduino Uno (Rev3)
  IC1 = L293D [package=THT]
  start = screw terminal, 2 pins
  R1 = Resistor [tolerance=±5% resistance=10k package=THT]
  back = screw terminal, 2 pins
  R2 = Resistor [tolerance=±5% resistance=10k package=THT]
  front = screw terminal, 2 pins
  R3 = Resistor [tolerance=±5% resistance=10k package=THT]
  motor = Screw terminal - 2 pins [package=THT]
  C1 = Ceramic Capacitor [capacitance=0.1µF package="100 mil [THT, multilayer]"]
  C2 = Ceramic Capacitor [capacitance=0.1µF package="100 mil [THT, multilayer]"]
  C4 = Electrolytic Capacitor [capacitance=4.7µF voltage=16V part_number=100uf package="100 mil [THT, electrolytic]"]
  Power_plug1 = Power plug - mod
  J1 = screw terminal, 8 pins

nets:
  N1: Part1.A0, J1.pin1
  N2: Part1.A1, J1.pin2
  N3: Part1.A2, J1.pin3
  N4: Part1.A3, J1.pin4
  N5: Part1.A4/SDA, J1.pin5
  N6: Part1.A5/SCL, J1.pin6
  N7: Part1.D8, IC1.In_1
  N8: Part1.D9_PWM, IC1.In_2
  N9: Part1.D2, start.pin1, R1.Pin_0
  N10: Part1.D4, back.pin1, R2.Pin_0
  N11: Part1.D7, front.pin1, R3.Pin_0
  N12: Part1.5V, IC1.Enable_1, IC1.+V, start.pin2, back.pin2, front.pin2, J1.pin7
  GND: Part1.GND, IC1.0V, R1.Pin_1, R2.Pin_1, R3.Pin_1, C1.0, C2.1, C4.-, Power_plug1.GND, J1.pin8
  N13: IC1.Out_1_(_Controlled_by_Enable_1_), motor.pin1, C1.1
  N14: IC1.Out_2_(_Controlled_by_Enable_1_), motor.pin2, C2.0
  N15: IC1.+Vmotor, C4.+, Power_plug1.VCC

notes:
  decoder v 0.2
  mz
  2014

custom parts:
  Power plug - mod: power plug
